# Fritzing sketch MCU-arduino_pro_mini (saved by Fritzing 0.9.3b)
breadboards: 1

parts:
  Mini_Pro = Arduino Mini (Rev5)

nets:
  net label: Mini_Pro.D2
  PIR_sensor: Mini_Pro.D3_PWM
  temperature_sensor: Mini_Pro.D4
  address0: Mini_Pro.D5_PWM
  address1: Mini_Pro.D6_PWM
  address3: Mini_Pro.D8
  relay0: Mini_Pro.D9_PWM
  relay3: Mini_Pro.A3
  soil_sensor: Mini_Pro.A2
  relay2: Mini_Pro.A1
  relay1: Mini_Pro.A0
  light_sensor: Mini_Pro.A6
  switch_input0: Mini_Pro.A4
  water_sensor: Mini_Pro.A7
  switch_input1: Mini_Pro.A5
  address2: Mini_Pro.RESET
  TX: Mini_Pro.TX
  RX: Mini_Pro.RX
  GND: Mini_Pro.GND
  5V: Mini_Pro.5V
